# Fritzing sketch raspberryPiTeleprompter (saved by Fritzing 0.9.4)

parts:
  Part1 = Adafruit Perma-Proto HAT [part_number="Adafruit #2314 and #2310"]
  Part2 = Adafruit TFP401 to 40 pin TFT (no Touch) [part_number="Adafruit #2218"]
  S1 = Pushbutton [package="[THT]"]
  S2 = Pushbutton [package="[THT]"]
  S3 = Pushbutton [package="[THT]"]
  S4 = Toggle Switch [package=THT]

nets:
  N1: Part1.GPIO4, Part1.N$59, S3.Pin_1, S3.Pin_2
  N2: Part1.GPIO17, Part1.N$56, S2.Pin_1, S2.Pin_2
  N3: Part1.GPIO18, Part1.N$41, S1.Pin_1, S1.Pin_2
  N4: Part1.GPIO27, Part1.N$4, S4.COM
  N5: Part1.5.0V, Part2.5V_PWR
  GND: Part1.GND, Part1.N$5, Part1.N$43, Part1.N$58, Part1.N$62, Part2.GND, S1.Pin_3, S1.Pin_4, S2.Pin_3, S2.Pin_4, S3.Pin_3, S3.Pin_4, S4.L2
  N6: Part1.N$3, S4.L1

custom parts:
  Adafruit Perma-Proto HAT: To kick off the Adafruit HAT party, we have this Perma-Proto inspired plug in daughter board. It has a grid of 0.1" prototyping soldering holes for attaching chips, resistors, LED, potentiometers and more. The holes are connected underneath with traces to mimic the solderless breadboards you're familiar. There's also long power strips for +3V, +5V and Ground connections to the Pi. Near the top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
  Adafruit TFP401 to 40 pin TFT (no Touch): It's a mini HDMI decoder board! So small and simple, you can use this board as an all-in-one display driver for TTL displays, or perhaps decoding HDMI/DVI video for some other project. This breakout features the TFP401 for decoding video, and for the touch version, an AR1100 USB resistive touch screen driver. The TFP401 is a beefy DVI/HDMI decoder from TI. It can take unencrypted video and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
